// Logisim project Bugputer.circ as structural Verilog: 4 circuits, main circuit main
module main (
  input  in_1,
  input  in_2,
  output [7:0] out_3
);

  _8_bit_Counter__100_Tick u_8_bit_counter_100_tick_1 (.\input (in_1), .reset(in_2), .count(out_3));
endmodule

module Switch__4_Tick (
  input  Input,
  input  Reset,
  output Output
);

  wire not_1_out, or_1_out, or_2_out, or_3_out, or_4_out;

  buf or_1 (or_1_out, Reset);  // OR_Gate
  buf or_2 (or_2_out, Input);  // OR_Gate
  or or_3 (or_3_out, or_1_out, Reset);
  not not_1 (not_1_out, or_3_out);
  or or_4 (or_4_out, Input, or_2_out, Output);
  and and_1 (Output, or_4_out, not_1_out);
endmodule

module Toggle__11_Tick (
  input  toggle,
  input  reset,
  output out_3
);

  wire and_1_out, and_2_out, and_3_out, not_1_out, not_2_out, or_1_out;

  not not_1 (not_1_out, toggle);
  not not_2 (not_2_out, toggle);
  and and_1 (and_1_out, toggle, not_1_out);
  Switch__4_Tick switch_4_tick_1 (.Input(and_1_out), .Reset(or_1_out), .Output(out_3));
  or or_1 (or_1_out, and_3_out, reset);
  and and_2 (and_2_out, not_2_out, out_3);
  and and_3 (and_3_out, and_2_out, toggle);
endmodule

module _8_bit_Counter__100_Tick (
  input  \input ,
  input  reset,
  output [7:0] count
);

  wire toggle_11_tick_1_out_3, toggle_11_tick_2_out_3, toggle_11_tick_3_out_3, toggle_11_tick_4_out_3,
       toggle_11_tick_5_out_3, toggle_11_tick_6_out_3, toggle_11_tick_7_out_3, toggle_11_tick_8_out_3;

  Toggle__11_Tick toggle_11_tick_1 (.toggle(\input ), .reset(reset), .out_3(toggle_11_tick_1_out_3));
  Toggle__11_Tick toggle_11_tick_2 (.toggle(toggle_11_tick_1_out_3), .reset(reset), .out_3(toggle_11_tick_2_out_3));
  Toggle__11_Tick toggle_11_tick_3 (.toggle(toggle_11_tick_4_out_3), .reset(reset), .out_3(toggle_11_tick_3_out_3));
  Toggle__11_Tick toggle_11_tick_4 (.toggle(toggle_11_tick_2_out_3), .reset(reset), .out_3(toggle_11_tick_4_out_3));
  Toggle__11_Tick toggle_11_tick_5 (.toggle(toggle_11_tick_3_out_3), .reset(reset), .out_3(toggle_11_tick_5_out_3));
  Toggle__11_Tick toggle_11_tick_6 (.toggle(toggle_11_tick_5_out_3), .reset(reset), .out_3(toggle_11_tick_6_out_3));
  Toggle__11_Tick toggle_11_tick_7 (.toggle(toggle_11_tick_8_out_3), .reset(reset), .out_3(toggle_11_tick_7_out_3));
  Toggle__11_Tick toggle_11_tick_8 (.toggle(toggle_11_tick_6_out_3), .reset(reset), .out_3(toggle_11_tick_8_out_3));
  not not_1 (count[0], toggle_11_tick_1_out_3);
  not not_2 (count[1], toggle_11_tick_2_out_3);
  not not_3 (count[2], toggle_11_tick_4_out_3);
  not not_4 (count[3], toggle_11_tick_3_out_3);
  not not_5 (count[4], toggle_11_tick_5_out_3);
  not not_6 (count[5], toggle_11_tick_6_out_3);
  not not_7 (count[6], toggle_11_tick_8_out_3);
  not not_8 (count[7], toggle_11_tick_7_out_3);
endmodule
