// Logisim project meecrosoft.circ as structural Verilog: 6 circuits, main circuit main
module main (
  input  in_1,
  input  in_2,
  output out_3,
  output out_4
);

  wire or_1_out;
  wire [6:0] keyboard_1_data;

  buf or_1 (or_1_out, in_2);  // OR_Gate
  Keyboard keyboard_1 (.clk(or_1_out), .data(keyboard_1_data));  // open: re, clr, avail
  TTY tty_1 (.data(keyboard_1_data), .clk(in_2));  // open: we, clr

  assign out_3 = in_1;
  assign out_4 = in_1;

  // Other names for the same wires on the sheet: h = in_1
endmodule

module bit__5_ticks (
  input  in,
  input  reset,
  output out
);

  wire not_2_out, or_1_out, or_2_out;

  or or_1 (or_1_out, reset, not_2_out);
  not not_1 (out, or_1_out);
  or or_2 (or_2_out, out, in);
  not not_2 (not_2_out, or_2_out);
endmodule

module byte__8_ticks (
  input  [7:0] in_1,
  input  in_2,
  output [7:0] out_3
);

  bit__5_ticks bit_5_ticks_1 (.in(in_1[0]), .reset(in_2), .out(out_3[0]));
  bit__5_ticks bit_5_ticks_2 (.in(in_1[1]), .reset(in_2), .out(out_3[1]));
  bit__5_ticks bit_5_ticks_3 (.in(in_1[2]), .reset(in_2), .out(out_3[2]));
  bit__5_ticks bit_5_ticks_4 (.in(in_1[3]), .reset(in_2), .out(out_3[3]));
  bit__5_ticks bit_5_ticks_5 (.in(in_1[4]), .reset(in_2), .out(out_3[4]));
  bit__5_ticks bit_5_ticks_6 (.in(in_1[5]), .reset(in_2), .out(out_3[5]));
  bit__5_ticks bit_5_ticks_7 (.in(in_1[6]), .reset(in_2), .out(out_3[6]));
  bit__5_ticks bit_5_ticks_8 (.in(in_1[7]), .reset(in_2), .out(out_3[7]));
endmodule

module instruction_decoder__4_ticks (
  input  [7:0] in_1,
  output out_2,
  output out_3,
  output out_4
);

  and and_1 (out_2, in_1[0], ~in_1[1], ~in_1[2], ~in_1[3], ~in_1[4], ~in_1[5], ~in_1[6], ~in_1[7]);  // AND_Gate
  and and_2 (out_3, ~in_1[0], in_1[1], ~in_1[2], ~in_1[3], ~in_1[4], ~in_1[5], ~in_1[6], ~in_1[7]);  // AND_Gate
  and and_3 (out_4, in_1[0], in_1[1], ~in_1[2], ~in_1[3], ~in_1[4], ~in_1[5], ~in_1[6], ~in_1[7]);  // AND_Gate

  // Other names for the same wires on the sheet: _0 = in_1[0]; _1 = in_1[1]; _2 = in_1[2]; _3 = in_1[3]; _4 = in_1[4];
  //   _5 = in_1[5]; _6 = in_1[6]; _7 = in_1[7]
endmodule

module program_counter (
  input  tick,
  input  reset,
  output [15:0] instruction_position,
  output out_4
);

  wire and_1_out, bit_5_ticks_2_out, undriven;

  bit__5_ticks bit_5_ticks_1 (.in(and_1_out), .reset(reset), .out(out_4));
  and and_1 (and_1_out, undriven, bit_5_ticks_2_out);
  bit__5_ticks bit_5_ticks_2 (.reset(reset), .out(bit_5_ticks_2_out));  // open: in
endmodule

module counter (
  input  toggle,
  input  reset
);

  wire and_1_out, and_2_out, bit_5_ticks_1_out, or_1_out;

  and and_1 (and_1_out, ~toggle, ~bit_5_ticks_1_out);  // AND_Gate
  bit__5_ticks bit_5_ticks_1 (.in(and_1_out), .reset(or_1_out), .out(bit_5_ticks_1_out));
  or or_1 (or_1_out, reset, and_2_out);
  and and_2 (and_2_out, toggle, bit_5_ticks_1_out);
endmodule
