// Logisim project templeOS2.circ as structural Verilog: 7 circuits, main circuit main
module main (
);

  _16_byte_memory u_16_byte_memory_1 ();  // open: byte_input, store, read, reset, byte_output
endmodule

module bit_memory (
  input  in_1,
  input  in_2,
  input  in_3,
  input  in_4,
  output out_5
);

  wire and_1_out, not_1_out, not_2_out, or_1_out, or_2_out;

  and and_1 (and_1_out, in_4, in_2);
  not not_1 (not_1_out, or_2_out);
  not not_2 (not_2_out, or_1_out);
  or or_1 (or_1_out, and_1_out, not_1_out);
  or or_2 (or_2_out, in_3, not_2_out);
  and and_2 (out_5, in_1, or_1_out);
endmodule

module _8_bit_memory (
  input  read,
  input  [7:0] in_2,
  input  store,
  input  reset,
  output [7:0] out_5
);

  bit_memory bit_memory_1 (.in_2(in_2[0]), .in_3(reset), .out_5(out_5[0]), .in_1(read), .in_4(store));
  bit_memory bit_memory_2 (.in_2(in_2[1]), .in_3(reset), .out_5(out_5[1]), .in_1(read), .in_4(store));
  bit_memory bit_memory_3 (.in_2(in_2[2]), .in_3(reset), .out_5(out_5[2]), .in_1(read), .in_4(store));
  bit_memory bit_memory_4 (.in_2(in_2[3]), .in_3(reset), .out_5(out_5[3]), .in_1(read), .in_4(store));
  bit_memory bit_memory_5 (.in_2(in_2[4]), .in_3(reset), .out_5(out_5[4]), .in_1(read), .in_4(store));
  bit_memory bit_memory_6 (.in_2(in_2[5]), .in_3(reset), .out_5(out_5[5]), .in_1(read), .in_4(store));
  bit_memory bit_memory_7 (.in_2(in_2[6]), .in_3(reset), .out_5(out_5[6]), .in_1(read), .in_4(store));
  bit_memory bit_memory_8 (.in_2(in_2[7]), .in_3(reset), .out_5(out_5[7]), .in_1(read), .in_4(store));
endmodule

module _16_byte_memory (
  input  [7:0] read,
  input  [7:0] byte_input,
  input  [7:0] store,
  input  [7:0] reset,
  output [7:0] byte_output
);

  wire [7:0] n8_bit_memory_1_out_5, n8_bit_memory_2_out_5, n8_bit_memory_3_out_5, n8_bit_memory_4_out_5,
       n8_bit_memory_5_out_5, n8_bit_memory_6_out_5, n8_bit_memory_7_out_5, n8_bit_memory_8_out_5, undriven,
       undriven_2, undriven_3;

  _8_bit_memory u_8_bit_memory_1 (
    .in_2(byte_input), .store(store[0]), .out_5(n8_bit_memory_1_out_5), .read(read[0]), .reset(reset[0]));
  _8_bit_memory u_8_bit_memory_2 (
    .in_2(undriven), .store(store[2]), .out_5(n8_bit_memory_2_out_5), .read(read[2]), .reset(reset[2]));
  _8_bit_memory u_8_bit_memory_3 (
    .in_2(byte_input), .store(store[1]), .out_5(n8_bit_memory_3_out_5), .read(read[1]), .reset(reset[1]));
  _8_bit_memory u_8_bit_memory_4 (
    .in_2(undriven), .store(store[3]), .out_5(n8_bit_memory_4_out_5), .read(read[3]), .reset(reset[3]));
  _8_bit_memory u_8_bit_memory_5 (
    .in_2(undriven_2), .store(store[4]), .out_5(n8_bit_memory_5_out_5), .read(read[4]), .reset(reset[4]));
  _8_bit_memory u_8_bit_memory_6 (
    .in_2(undriven_2), .store(store[5]), .out_5(n8_bit_memory_6_out_5), .read(read[5]), .reset(reset[5]));
  _8_bit_memory u_8_bit_memory_7 (
    .in_2(undriven_3), .store(store[6]), .out_5(n8_bit_memory_7_out_5), .read(read[6]), .reset(reset[6]));
  _8_bit_memory u_8_bit_memory_8 (
    .in_2(undriven_3), .store(store[7]), .out_5(n8_bit_memory_8_out_5), .read(read[7]), .reset(reset[7]));
  _8_byte_stream_converge u_8_byte_stream_converge_1 (
    .in_1(n8_bit_memory_8_out_5), .in_2(n8_bit_memory_7_out_5), .in_3(n8_bit_memory_6_out_5),
    .in_4(n8_bit_memory_5_out_5), .in_5(n8_bit_memory_4_out_5), .in_6(n8_bit_memory_2_out_5),
    .in_7(n8_bit_memory_3_out_5), .in_8(n8_bit_memory_1_out_5), .out_9(byte_output));
endmodule

module _1_way (
  input  [7:0] in_1,
  output [7:0] out_2
);


  assign out_2 = in_1;
endmodule

module _8_byte_stream_converge (
  input  [7:0] in_1,
  input  [7:0] in_2,
  input  [7:0] in_3,
  input  [7:0] in_4,
  input  [7:0] in_5,
  input  [7:0] in_6,
  input  [7:0] in_7,
  input  [7:0] in_8,
  output [7:0] out_9
);

  wire [7:0] n2_byte_stream_converge_1_out_3, n2_byte_stream_converge_2_out_3,
       n2_byte_stream_converge_3_out_3, n2_byte_stream_converge_4_out_3, n2_byte_stream_converge_5_out_3,
       n2_byte_stream_converge_7_out_3;

  _2_byte_stream_converge u_2_byte_stream_converge_1 (
    .in_1(in_1), .in_2(in_2), .out_3(n2_byte_stream_converge_1_out_3));
  _2_byte_stream_converge u_2_byte_stream_converge_2 (
    .in_1(in_3), .in_2(in_4), .out_3(n2_byte_stream_converge_2_out_3));
  _2_byte_stream_converge u_2_byte_stream_converge_3 (
    .in_1(in_5), .in_2(in_6), .out_3(n2_byte_stream_converge_3_out_3));
  _2_byte_stream_converge u_2_byte_stream_converge_4 (
    .in_1(in_7), .in_2(in_8), .out_3(n2_byte_stream_converge_4_out_3));
  _2_byte_stream_converge u_2_byte_stream_converge_5 (
    .in_1(n2_byte_stream_converge_1_out_3), .in_2(n2_byte_stream_converge_2_out_3),
    .out_3(n2_byte_stream_converge_5_out_3));
  _2_byte_stream_converge u_2_byte_stream_converge_6 (
    .in_1(n2_byte_stream_converge_5_out_3), .in_2(n2_byte_stream_converge_7_out_3), .out_3(out_9));
  _2_byte_stream_converge u_2_byte_stream_converge_7 (
    .in_1(n2_byte_stream_converge_3_out_3), .in_2(n2_byte_stream_converge_4_out_3),
    .out_3(n2_byte_stream_converge_7_out_3));
endmodule

module _2_byte_stream_converge (
  input  [7:0] in_1,
  input  [7:0] in_2,
  output [7:0] out_3
);

  or or_1 (out_3[0], in_2[0], in_1[0]);
  or or_2 (out_3[1], in_2[1], in_1[1]);
  or or_3 (out_3[2], in_2[2], in_1[2]);
  or or_4 (out_3[3], in_2[3], in_1[3]);
  or or_5 (out_3[4], in_2[4], in_1[4]);
  or or_6 (out_3[5], in_2[5], in_1[5]);
  or or_7 (out_3[6], in_2[6], in_1[6]);
  or or_8 (out_3[7], in_2[7], in_1[7]);
endmodule
